// Logisim project mips_pipeline.circ as structural Verilog: 13 circuits, main circuit main
module main (
);

  wire and_1_out, and_2_out, branch_jump_unit_1_pcmux, clock_1_out, hazard_unit_1_can_advance,
       hazard_unit_1_clear_ex_mem__nop, hazard_unit_1_hazard_detected, hazard_unit_1_rs_data_src,
       hazard_unit_1_rt_data_src, reg_ex_mem_1_branch_2, reg_ex_mem_1_jump_2, reg_ex_mem_1_memory_write_2,
       reg_ex_mem_1_memtoreg_2, reg_ex_mem_1_regwrite_2, reg_ex_mem_1_type_2, reg_ex_mem_1_zero_2,
       reg_id_ex_1_alusrc_2, reg_id_ex_1_branch_2, reg_id_ex_1_jump_2, reg_id_ex_1_memtoreg_2,
       reg_id_ex_1_memwrite_2, reg_id_ex_1_regdest_2, reg_id_ex_1_regwrite_2, reg_id_ex_1_set_2,
       reg_id_ex_1_type_2, reg_mem_wb_1_jump_2, reg_mem_wb_1_memtoreg_2, reg_mem_wb_1_reg_write_2,
       uc_w_1_alusrc, uc_w_1_branch, uc_w_1_jump, uc_w_1_memtoreg, uc_w_1_memwrite, uc_w_1_regdest,
       uc_w_1_regwrite, uc_w_1_set, uc_w_1_type, ula_1_igual;
  wire [2:0] reg_id_ex_1_aluop_2, uc_w_1_aluop;
  wire [4:0] multiplexer_5_out, multiplexer_8_out, reg_ex_mem_1_write_register_2, reg_id_ex_1_rd_2,
       reg_id_ex_1_rs_2, reg_id_ex_1_rt_2, reg_mem_wb_1_write_register_2;
  wire [5:0] alu_control_1_out_3;
  wire [31:0] adder_1_out, adder_2_out, banco_registradores_1_r1, banco_registradores_1_r2,
       bit_extender_1_out, bit_extender_2_out, branch_jump_unit_1_address, DATA_MEMORY_data,
       hazard_unit_1_fixed_data_rs, hazard_unit_1_fixed_data_rt, INSTRUCTION_MEMORY_data, multiplexer_1_out,
       multiplexer_2_out, multiplexer_3_out, multiplexer_4_out, multiplexer_6_out, multiplexer_7_out,
       multiplexer_9_out, PC_q, reg_ex_mem_1_alu_out_2, reg_ex_mem_1_branch_address_2,
       reg_ex_mem_1_data_rt_2, reg_ex_mem_1_ins_2, reg_ex_mem_1_label_2, reg_ex_mem_1_pc_4_2,
       reg_id_ex_1_data_rs_2, reg_id_ex_1_data_rt_2, reg_id_ex_1_imext_2, reg_id_ex_1_ins_2,
       reg_id_ex_1_label_2, reg_id_ex_1_pc_4_2, reg_if_id_1_out_5, reg_if_id_1_out_6, reg_mem_wb_1_alu_out_2,
       reg_mem_wb_1_ins_2, reg_mem_wb_1_mem_out_2, reg_mem_wb_1_pc_4_2, shifter_1_out, shifter_2_out,
       ula_1_resultado;

  Multiplexer #(.width(32), .enable("false")) multiplexer_1 (
    .in0(adder_1_out), .in1(branch_jump_unit_1_address), .out(multiplexer_1_out),
    .sel(branch_jump_unit_1_pcmux));
  and and_1 (and_1_out, clock_1_out, hazard_unit_1_can_advance);
  Adder #(.width(32)) adder_1 (.a(32'h4), .b(PC_q), .out(adder_1_out));  // open: cin, cout
  Register #(.width(32), .Select("low")) PC (.D(multiplexer_1_out), .Q(PC_q), .clk(and_1_out));  // open: en, clr
  RAM #(.addrWidth(16), .dataWidth(32), .Select("high"), .simpleMode("false")) INSTRUCTION_MEMORY (
    .addr(PC_q[17:2]), .data(INSTRUCTION_MEMORY_data), .clk(clock_1_out));  // open: sel, ld, clr
  REG_IF_ID reg_if_id_1 (
    .in_1(adder_1_out), .in_2(INSTRUCTION_MEMORY_data), .out_5(reg_if_id_1_out_5), .out_6(reg_if_id_1_out_6),
    .CLK(clock_1_out), .CANADVANCE(hazard_unit_1_can_advance));
  UC_W uc_w_1 (
    .in_1(reg_if_id_1_out_6[31:26]), .REGDEST(uc_w_1_regdest), .JUMP(uc_w_1_jump), .BRANCH(uc_w_1_branch),
    .MEMTOREG(uc_w_1_memtoreg), .ALUOP(uc_w_1_aluop), .MEMWRITE(uc_w_1_memwrite), .ALUSRC(uc_w_1_alusrc),
    .REGWRITE(uc_w_1_regwrite), .SET(uc_w_1_set), .TYPE(uc_w_1_type));
  banco_registradores banco_registradores_1 (
    .R1_num(reg_if_id_1_out_6[25:21]), .R2_num(reg_if_id_1_out_6[20:16]), .RW(multiplexer_8_out),
    .Din(multiplexer_9_out), .WE(reg_mem_wb_1_reg_write_2), .clk(clock_1_out), .R1(banco_registradores_1_r1),
    .R2(banco_registradores_1_r2));
  assign bit_extender_1_out = {{16{reg_if_id_1_out_6[15]}}, reg_if_id_1_out_6[15:0]};  // Bit_Extender bit_extender_1
  assign bit_extender_2_out = {{6{reg_if_id_1_out_6[25]}}, reg_if_id_1_out_6[25:0]};  // Bit_Extender bit_extender_2
  Clock clock_1 (.out(clock_1_out));
  REG_ID_EX reg_id_ex_1 (
    .RegDest(uc_w_1_regdest), .Branch(uc_w_1_branch), .MemtoReg(uc_w_1_memtoreg), .ALUOp(uc_w_1_aluop),
    .ALUSrc(uc_w_1_alusrc), .RegWrite(uc_w_1_regwrite), .PC_4(reg_if_id_1_out_5),
    .DATA_RS(banco_registradores_1_r1), .DATA_RT(banco_registradores_1_r2), .IMEXT(bit_extender_1_out),
    .RT(reg_if_id_1_out_6[20:16]), .RD(reg_if_id_1_out_6[15:11]), .RegDest_2(reg_id_ex_1_regdest_2),
    .Branch_2(reg_id_ex_1_branch_2), .MemtoReg_2(reg_id_ex_1_memtoreg_2), .ALUOp_2(reg_id_ex_1_aluop_2),
    .ALUSrc_2(reg_id_ex_1_alusrc_2), .RegWrite_2(reg_id_ex_1_regwrite_2), .PC_4_2(reg_id_ex_1_pc_4_2),
    .DATA_RS_2(reg_id_ex_1_data_rs_2), .DATA_RT_2(reg_id_ex_1_data_rt_2), .IMEXT_2(reg_id_ex_1_imext_2),
    .RT_2(reg_id_ex_1_rt_2), .RD_2(reg_id_ex_1_rd_2), .CLK(clock_1_out), .MemWrite(uc_w_1_memwrite),
    .MemWrite_2(reg_id_ex_1_memwrite_2), .TYPE(uc_w_1_type), .TYPE_2(reg_id_ex_1_type_2),
    .LABEL(bit_extender_2_out), .LABEL_2(reg_id_ex_1_label_2), .JUMP(uc_w_1_jump),
    .JUMP_2(reg_id_ex_1_jump_2), .SET(uc_w_1_set), .SET_2(reg_id_ex_1_set_2), .RS(reg_if_id_1_out_6[25:21]),
    .RS_2(reg_id_ex_1_rs_2), .CanAdvance(hazard_unit_1_can_advance), .INS(reg_if_id_1_out_6),
    .INS_2(reg_id_ex_1_ins_2));
  Multiplexer #(.width(32), .enable("false")) multiplexer_2 (
    .in0(reg_id_ex_1_data_rs_2), .in1(hazard_unit_1_fixed_data_rs), .out(multiplexer_2_out),
    .sel(hazard_unit_1_rs_data_src));
  Multiplexer #(.width(32), .enable("false")) multiplexer_3 (
    .in0(reg_id_ex_1_data_rt_2), .in1(hazard_unit_1_fixed_data_rt), .out(multiplexer_3_out),
    .sel(hazard_unit_1_rt_data_src));
  Hazard_Unit hazard_unit_1 (
    .RS_ID(reg_id_ex_1_rs_2), .RT_ID(reg_id_ex_1_rt_2), .WR_EX_MEM(reg_ex_mem_1_write_register_2),
    .WR_MEM_WB(reg_mem_wb_1_write_register_2), .RT_DATA_SRC(hazard_unit_1_rt_data_src),
    .RS_DATA_SRC(hazard_unit_1_rs_data_src), .CLEAR_EX_MEM__NOP(hazard_unit_1_clear_ex_mem__nop),
    .MEMTOREG_EX_MEM(reg_ex_mem_1_memtoreg_2), .CAN_ADVANCE(hazard_unit_1_can_advance),
    .FIXED_DATA_RS(hazard_unit_1_fixed_data_rs), .ALUOUT_EX_MEM(reg_ex_mem_1_alu_out_2),
    .DATAOUT_MEM_WB(multiplexer_7_out), .REGWRITE_EX_MEM(reg_ex_mem_1_regwrite_2),
    .HAZARD_DETECTED(hazard_unit_1_hazard_detected), .REGWRITE_MEM_WB(reg_mem_wb_1_reg_write_2),
    .INS(reg_id_ex_1_ins_2), .INS_EX_MEM(reg_ex_mem_1_ins_2), .CLK(clock_1_out),
    .INS_MEM_WB(reg_mem_wb_1_ins_2), .FIXED_DATA_RT(hazard_unit_1_fixed_data_rt));
  Multiplexer #(.width(32), .enable("false")) multiplexer_4 (
    .in0(multiplexer_3_out), .in1(reg_id_ex_1_imext_2), .out(multiplexer_4_out), .sel(reg_id_ex_1_alusrc_2));
  Multiplexer #(.width(5), .enable("false")) multiplexer_5 (
    .in0(reg_id_ex_1_rt_2), .in1(reg_id_ex_1_rd_2), .out(multiplexer_5_out), .sel(reg_id_ex_1_regdest_2));
  ALU_CONTROL alu_control_1 (.in_1(reg_id_ex_1_imext_2[5:0]), .out_3(alu_control_1_out_3), .in_2(reg_id_ex_1_aluop_2));
  Shifter #(.width(32)) shifter_1 (.in(reg_id_ex_1_imext_2), .\dist (5'b00010), .out(shifter_1_out));
  ULA ula_1 (
    .A(multiplexer_2_out), .B(multiplexer_4_out), .Resultado(ula_1_resultado), .OP(alu_control_1_out_3),
    .igual(ula_1_igual), .Shamt(reg_id_ex_1_imext_2[10:6]), .SET(reg_id_ex_1_set_2));
  LED led_1 (.in(hazard_unit_1_hazard_detected));
  Adder #(.width(32)) adder_2 (.a(reg_id_ex_1_pc_4_2), .b(shifter_1_out), .out(adder_2_out));  // open: cin, cout
  and and_2 (and_2_out, reg_id_ex_1_jump_2, reg_id_ex_1_type_2);
  Multiplexer #(.width(32), .enable("false")) multiplexer_6 (
    .in0(adder_2_out), .in1(multiplexer_2_out), .out(multiplexer_6_out), .sel(and_2_out));
  REG_EX_MEM reg_ex_mem_1 (
    .BRANCH(reg_id_ex_1_branch_2), .MEMTOREG(reg_id_ex_1_memtoreg_2), .MEMORY_WRITE(reg_id_ex_1_memwrite_2),
    .REGWRITE(reg_id_ex_1_regwrite_2), .BRANCH_ADDRESS(multiplexer_6_out), .zero(ula_1_igual),
    .ALU_OUT(ula_1_resultado), .DATA_RT(multiplexer_3_out), .WRITE_REGISTER(multiplexer_5_out),
    .BRANCH_2(reg_ex_mem_1_branch_2), .MEMTOREG_2(reg_ex_mem_1_memtoreg_2),
    .MEMORY_WRITE_2(reg_ex_mem_1_memory_write_2), .REGWRITE_2(reg_ex_mem_1_regwrite_2),
    .BRANCH_ADDRESS_2(reg_ex_mem_1_branch_address_2), .zero_2(reg_ex_mem_1_zero_2),
    .ALU_OUT_2(reg_ex_mem_1_alu_out_2), .DATA_RT_2(reg_ex_mem_1_data_rt_2),
    .WRITE_REGISTER_2(reg_ex_mem_1_write_register_2), .CLK(clock_1_out), .TYPE(reg_id_ex_1_type_2),
    .TYPE_2(reg_ex_mem_1_type_2), .LABEL(shifter_2_out), .LABEL_2(reg_ex_mem_1_label_2),
    .JUMP(reg_id_ex_1_jump_2), .JUMP_2(reg_ex_mem_1_jump_2), .PC_4(reg_id_ex_1_pc_4_2),
    .PC_4_2(reg_ex_mem_1_pc_4_2), .Clear(hazard_unit_1_clear_ex_mem__nop),
    .CanAdvance(hazard_unit_1_can_advance), .INS(reg_id_ex_1_ins_2), .INS_2(reg_ex_mem_1_ins_2));
  Shifter #(.width(32)) shifter_2 (.in(reg_id_ex_1_label_2), .\dist (5'b00010), .out(shifter_2_out));
  Branch_Jump_Unit branch_jump_unit_1 (
    .BRANCH(reg_ex_mem_1_branch_2), .EQUAL(reg_ex_mem_1_zero_2), .PCMUX(branch_jump_unit_1_pcmux),
    .ADDRESS(branch_jump_unit_1_address), .IMADDRESS(reg_ex_mem_1_branch_address_2),
    .LABELADDRESS(reg_ex_mem_1_label_2), .JUMP(reg_ex_mem_1_jump_2), .TYPE(reg_ex_mem_1_type_2));
  RAM #(.addrWidth(16), .dataWidth(32), .bus("separate"), .Select("high"), .simpleMode("false")) DATA_MEMORY (
    .addr(reg_ex_mem_1_alu_out_2[17:2]), .din(reg_ex_mem_1_data_rt_2), .data(DATA_MEMORY_data),
    .str(reg_ex_mem_1_memory_write_2), .clk(clock_1_out));  // open: sel, ld, clr
  REG_MEM_WB reg_mem_wb_1 (
    .REG_WRITE(reg_ex_mem_1_regwrite_2), .MEMTOREG(reg_ex_mem_1_memtoreg_2), .MEM_OUT(DATA_MEMORY_data),
    .ALU_OUT(reg_ex_mem_1_alu_out_2), .WRITE_REGISTER(reg_ex_mem_1_write_register_2),
    .REG_WRITE_2(reg_mem_wb_1_reg_write_2), .MEMTOREG_2(reg_mem_wb_1_memtoreg_2),
    .MEM_OUT_2(reg_mem_wb_1_mem_out_2), .ALU_OUT_2(reg_mem_wb_1_alu_out_2),
    .WRITE_REGISTER_2(reg_mem_wb_1_write_register_2), .CLK(clock_1_out), .JUMP(reg_ex_mem_1_jump_2),
    .JUMP_2(reg_mem_wb_1_jump_2), .PC_4(reg_ex_mem_1_pc_4_2), .PC_4_2(reg_mem_wb_1_pc_4_2),
    .INS(reg_ex_mem_1_ins_2), .INS_2(reg_mem_wb_1_ins_2));
  Multiplexer #(.width(32), .enable("false")) multiplexer_7 (
    .in0(reg_mem_wb_1_alu_out_2), .in1(reg_mem_wb_1_mem_out_2), .out(multiplexer_7_out),
    .sel(reg_mem_wb_1_memtoreg_2));
  Multiplexer #(.width(5), .enable("false")) multiplexer_8 (
    .in0(reg_mem_wb_1_write_register_2), .in1({5{1'b1}}), .out(multiplexer_8_out), .sel(reg_mem_wb_1_jump_2));
  Multiplexer #(.width(32), .enable("false")) multiplexer_9 (
    .in0(multiplexer_7_out), .in1(reg_mem_wb_1_pc_4_2), .out(multiplexer_9_out), .sel(reg_mem_wb_1_jump_2));

  // Notes on the sheet:
  //   IF-ID
  //   RegDest
  //   Jump
  //   Branch
  //   MemtoReg
  //   ALUOp
  //   MemWrite
  //   ALUSrc
  //   RegWrite
  //   Type
  //   Set
  //   ID-EX
  //   RT ID-EX
  //   INS
  //   RS ID-EX
  //   REGWRITE MEM-WB
  //   REGWRITE EX-MEM
  //   MEMTOREG EX-MEM
  //   INS FOR DEBUG
  //   DATAOUT MEM-WB
  //   ALUOUT EX-MEM
  //   WR EX-MEM
  //   WR MEM-WB
  //   HAZARD DETECTED?
  //   Instruções não nulas que não alteram nada
  //   as vezes geram falsos hazards pois acabam comparando
  //   parte RD do imediato com registradores zerados e etc.
  //   São apenas alarmes falsos e não atrapalham em nada.
  //   EX-MEM
  //   DEBUG
  //   MEM-WB
endmodule

module banco_registradores (
  input  [4:0] R1_num,
  input  [4:0] R2_num,
  input  [4:0] RW,
  input  [31:0] Din,
  input  WE,
  input  clk,
  output [31:0] R1,
  output [31:0] R2
);

  wire demultiplexer_1_out0, demultiplexer_1_out1, demultiplexer_1_out2, demultiplexer_1_out3,
       demultiplexer_2_out0, demultiplexer_2_out1, demultiplexer_2_out2, demultiplexer_2_out3,
       demultiplexer_2_out4, demultiplexer_2_out5, demultiplexer_2_out6, demultiplexer_2_out7,
       demultiplexer_3_out0, demultiplexer_3_out1, demultiplexer_3_out2, demultiplexer_3_out3,
       demultiplexer_3_out4, demultiplexer_3_out5, demultiplexer_3_out6, demultiplexer_3_out7,
       demultiplexer_4_out0, demultiplexer_4_out1, demultiplexer_4_out2, demultiplexer_4_out3,
       demultiplexer_4_out4, demultiplexer_4_out5, demultiplexer_4_out6, demultiplexer_4_out7,
       demultiplexer_5_out0, demultiplexer_5_out1, demultiplexer_5_out2, demultiplexer_5_out3,
       demultiplexer_5_out4, demultiplexer_5_out5, demultiplexer_5_out6, demultiplexer_5_out7;
  wire [31:0] _0__Zero_q, _1__at_q, _3__v1_q, _5__a1_q, _6__a2_q, _7__a3_q, _8__t0_q, _9__t1_q, _10__t2_q,
       _11__t3_q, _12__t4_q, _13__t5_q, _14__t6_q, _15__t7_q, _19__s3_q, _20__s4_q, _21__s5_q, _22__s6_q,
       _23__s7_q, _24__t8_q, _25__t9_q, _26__k0_q, _27__k1_q, _28__gp_q, _29__sp_q, _30__fp_q, a0, ra, s0,
       s1, s2, v0;

  Demultiplexer #(.select(2), .disabled(0)) demultiplexer_1 (
    .out0(demultiplexer_1_out0), .out1(demultiplexer_1_out1), .out2(demultiplexer_1_out2),
    .out3(demultiplexer_1_out3), .in(1'b1), .sel(RW[4:3]), .en(WE));
  Demultiplexer #(.select(3), .disabled(0)) demultiplexer_2 (
    .out0(demultiplexer_2_out0), .out1(demultiplexer_2_out1), .out2(demultiplexer_2_out2),
    .out3(demultiplexer_2_out3), .out4(demultiplexer_2_out4), .out5(demultiplexer_2_out5),
    .out6(demultiplexer_2_out6), .out7(demultiplexer_2_out7), .in(1'b1), .sel(RW[2:0]),
    .en(demultiplexer_1_out0));
  Demultiplexer #(.select(3), .disabled(0)) demultiplexer_3 (
    .out0(demultiplexer_3_out0), .out1(demultiplexer_3_out1), .out2(demultiplexer_3_out2),
    .out3(demultiplexer_3_out3), .out4(demultiplexer_3_out4), .out5(demultiplexer_3_out5),
    .out6(demultiplexer_3_out6), .out7(demultiplexer_3_out7), .in(1'b1), .sel(RW[2:0]),
    .en(demultiplexer_1_out1));
  Demultiplexer #(.select(3), .disabled(0)) demultiplexer_4 (
    .out0(demultiplexer_4_out0), .out1(demultiplexer_4_out1), .out2(demultiplexer_4_out2),
    .out3(demultiplexer_4_out3), .out4(demultiplexer_4_out4), .out5(demultiplexer_4_out5),
    .out6(demultiplexer_4_out6), .out7(demultiplexer_4_out7), .in(1'b1), .sel(RW[2:0]),
    .en(demultiplexer_1_out2));
  Demultiplexer #(.select(3), .disabled(0)) demultiplexer_5 (
    .out0(demultiplexer_5_out0), .out1(demultiplexer_5_out1), .out2(demultiplexer_5_out2),
    .out3(demultiplexer_5_out3), .out4(demultiplexer_5_out4), .out5(demultiplexer_5_out5),
    .out6(demultiplexer_5_out6), .out7(demultiplexer_5_out7), .in(1'b1), .sel(RW[2:0]),
    .en(demultiplexer_1_out3));
  Register #(.width(32), .Select("low")) _0__Zero (
    .D(Din), .en(demultiplexer_2_out0), .Q(_0__Zero_q));  // open: clk, clr
  Register #(.width(32), .Select("low")) _8__t0 (
    .D(Din), .en(demultiplexer_3_out0), .Q(_8__t0_q), .clk(clk));  // open: clr
  Register #(.width(32), .Select("low")) _16__s0 (.D(Din), .en(demultiplexer_4_out0), .Q(s0), .clk(clk));  // open: clr
  Register #(.width(32), .Select("low")) _24__t8 (
    .D(Din), .en(demultiplexer_5_out0), .Q(_24__t8_q), .clk(clk));  // open: clr
  Register #(.width(32), .Select("low")) _1__at (
    .D(Din), .en(demultiplexer_2_out1), .Q(_1__at_q), .clk(clk));  // open: clr
  Register #(.width(32), .Select("low")) _9__t1 (
    .D(Din), .en(demultiplexer_3_out1), .Q(_9__t1_q), .clk(clk));  // open: clr
  Register #(.width(32), .Select("low")) _17__s1 (.D(Din), .en(demultiplexer_4_out1), .Q(s1), .clk(clk));  // open: clr
  Register #(.width(32), .Select("low")) _25__t9 (
    .D(Din), .en(demultiplexer_5_out1), .Q(_25__t9_q), .clk(clk));  // open: clr
  Register #(.width(32), .Select("low")) _2__v0 (.D(Din), .en(demultiplexer_2_out2), .Q(v0), .clk(clk));  // open: clr
  Register #(.width(32), .Select("low")) _10__t2 (
    .D(Din), .en(demultiplexer_3_out2), .Q(_10__t2_q), .clk(clk));  // open: clr
  Register #(.width(32), .Select("low")) _18__s2 (.D(Din), .en(demultiplexer_4_out2), .Q(s2), .clk(clk));  // open: clr
  Register #(.width(32), .Select("low")) _26__k0 (
    .D(Din), .en(demultiplexer_5_out2), .Q(_26__k0_q), .clk(clk));  // open: clr
  Register #(.width(32), .Select("low")) _3__v1 (
    .D(Din), .en(demultiplexer_2_out3), .Q(_3__v1_q), .clk(clk));  // open: clr
  Register #(.width(32), .Select("low")) _11__t3 (
    .D(Din), .en(demultiplexer_3_out3), .Q(_11__t3_q), .clk(clk));  // open: clr
  Register #(.width(32), .Select("low")) _19__s3 (
    .D(Din), .en(demultiplexer_4_out3), .Q(_19__s3_q), .clk(clk));  // open: clr
  Register #(.width(32), .Select("low")) _27__k1 (
    .D(Din), .en(demultiplexer_5_out3), .Q(_27__k1_q), .clk(clk));  // open: clr
  Register #(.width(32), .Select("low")) _4__a0 (.D(Din), .en(demultiplexer_2_out4), .Q(a0), .clk(clk));  // open: clr
  Register #(.width(32), .Select("low")) _12__t4 (
    .D(Din), .en(demultiplexer_3_out4), .Q(_12__t4_q), .clk(clk));  // open: clr
  Register #(.width(32), .Select("low")) _20__s4 (
    .D(Din), .en(demultiplexer_4_out4), .Q(_20__s4_q), .clk(clk));  // open: clr
  Register #(.width(32), .Select("low")) _28__gp (
    .D(Din), .en(demultiplexer_5_out4), .Q(_28__gp_q), .clk(clk));  // open: clr
  Register #(.width(32), .Select("low")) _5__a1 (
    .D(Din), .en(demultiplexer_2_out5), .Q(_5__a1_q), .clk(clk));  // open: clr
  Register #(.width(32), .Select("low")) _13__t5 (
    .D(Din), .en(demultiplexer_3_out5), .Q(_13__t5_q), .clk(clk));  // open: clr
  Register #(.width(32), .Select("low")) _21__s5 (
    .D(Din), .en(demultiplexer_4_out5), .Q(_21__s5_q), .clk(clk));  // open: clr
  Register #(.width(32), .Select("low")) _29__sp (
    .D(Din), .en(demultiplexer_5_out5), .Q(_29__sp_q), .clk(clk));  // open: clr
  Register #(.width(32), .Select("low")) _6__a2 (
    .D(Din), .en(demultiplexer_2_out6), .Q(_6__a2_q), .clk(clk));  // open: clr
  Register #(.width(32), .Select("low")) _14__t6 (
    .D(Din), .en(demultiplexer_3_out6), .Q(_14__t6_q), .clk(clk));  // open: clr
  Register #(.width(32), .Select("low")) _22__s6 (
    .D(Din), .en(demultiplexer_4_out6), .Q(_22__s6_q), .clk(clk));  // open: clr
  Register #(.width(32), .Select("low")) _30__fp (
    .D(Din), .en(demultiplexer_5_out6), .Q(_30__fp_q), .clk(clk));  // open: clr
  Register #(.width(32), .Select("low")) _7__a3 (
    .D(Din), .en(demultiplexer_2_out7), .Q(_7__a3_q), .clk(clk));  // open: clr
  Register #(.width(32), .Select("low")) _15__t7 (
    .D(Din), .en(demultiplexer_3_out7), .Q(_15__t7_q), .clk(clk));  // open: clr
  Register #(.width(32), .Select("low")) _23__s7 (
    .D(Din), .en(demultiplexer_4_out7), .Q(_23__s7_q), .clk(clk));  // open: clr
  Register #(.width(32), .Select("low")) _31__ra (.D(Din), .en(demultiplexer_5_out7), .Q(ra), .clk(clk));  // open: clr
  Multiplexer #(.select(5), .width(32), .enable("false")) multiplexer_1 (
    .in0(_0__Zero_q), .in1(_1__at_q), .in2(v0), .in3(_3__v1_q), .in4(a0), .in5(_5__a1_q), .in6(_6__a2_q),
    .in7(_7__a3_q), .in8(_8__t0_q), .in9(_9__t1_q), .in10(_10__t2_q), .in11(_11__t3_q), .in12(_12__t4_q),
    .in13(_13__t5_q), .in14(_14__t6_q), .in15(_15__t7_q), .in16(s0), .in17(s1), .in18(s2), .in19(_19__s3_q),
    .in20(_20__s4_q), .in21(_21__s5_q), .in22(_22__s6_q), .in23(_23__s7_q), .in24(_24__t8_q),
    .in25(_25__t9_q), .in26(_26__k0_q), .in27(_27__k1_q), .in28(_28__gp_q), .in29(_29__sp_q),
    .in30(_30__fp_q), .in31(ra), .out(R1), .sel(R1_num));
  Multiplexer #(.select(5), .width(32), .enable("false")) multiplexer_2 (
    .in0(_0__Zero_q), .in1(_1__at_q), .in2(v0), .in3(_3__v1_q), .in4(a0), .in5(_5__a1_q), .in6(_6__a2_q),
    .in7(_7__a3_q), .in8(_8__t0_q), .in9(_9__t1_q), .in10(_10__t2_q), .in11(_11__t3_q), .in12(_12__t4_q),
    .in13(_13__t5_q), .in14(_14__t6_q), .in15(_15__t7_q), .in16(s0), .in17(s1), .in18(s2), .in19(_19__s3_q),
    .in20(_20__s4_q), .in21(_21__s5_q), .in22(_22__s6_q), .in23(_23__s7_q), .in24(_24__t8_q),
    .in25(_25__t9_q), .in26(_26__k0_q), .in27(_27__k1_q), .in28(_28__gp_q), .in29(_29__sp_q),
    .in30(_30__fp_q), .in31(ra), .out(R2), .sel(R2_num));

  // Other names for the same wires on the sheet: reg1[31:0] = R1; reg1_num[4:0] = R1_num; reg2[31:0] = R2;
  //   reg2_num[4:0] = R2_num; write_data[31:0] = Din; write_reg_num[4:0] = RW

  // Notes on the sheet:
  //   Input
  //   Output
endmodule

module ULA (
  input  [31:0] A,
  input  [31:0] B,
  input  SET,
  input  [5:0] OP,
  input  [4:0] Shamt,
  output [31:0] Resultado,
  output igual
);

  wire comparator_1_lt;
  wire [31:0] adder_1_out, AND_out, divider_1_out, multiplexer_1_out, multiplexer_2_out, multiplier_1_out,
       OR_out, shifter_1_out, shifter_2_out, subtractor_1_out;

  Adder #(.width(32)) adder_1 (.a(A), .b(B), .out(adder_1_out));  // open: cin, cout
  Subtractor #(.width(32)) subtractor_1 (.a(A), .b(B), .out(subtractor_1_out));  // open: bin, bout
  Multiplier #(.width(32)) multiplier_1 (.a(A), .b(B), .out(multiplier_1_out));  // open: cin, cout
  Divider #(.width(32)) divider_1 (.a(A), .b(B), .out(divider_1_out));  // open: upper, rem
  Comparator #(.width(32)) comparator_1 (.a(A), .b(B), .eq(igual), .lt(comparator_1_lt));  // open: gt
  assign AND_out = A & B;  // AND_Gate AND, 32 bits wide
  assign OR_out = A | B;  // OR_Gate OR, 32 bits wide
  Shifter #(.width(32)) shifter_1 (.in(A), .\dist (Shamt), .out(shifter_1_out));
  Shifter #(.width(32), .shift("lr")) shifter_2 (.in(A), .\dist (Shamt), .out(shifter_2_out));
  Multiplexer #(.select(3), .width(32), .enable("false")) multiplexer_1 (
    .in0(adder_1_out), .in1(subtractor_1_out), .in2(multiplier_1_out), .in3(divider_1_out), .in4(AND_out),
    .in5(OR_out), .in6(shifter_1_out), .in7(shifter_2_out), .out(multiplexer_1_out), .sel(OP[2:0]));
  Multiplexer #(.width(32), .enable("false")) multiplexer_2 (
    .in0({32{1'b0}}), .in1(32'h1), .out(multiplexer_2_out), .sel(comparator_1_lt));
  Multiplexer #(.width(32), .enable("false")) multiplexer_3 (
    .in0(multiplexer_1_out), .in1(multiplexer_2_out), .out(Resultado), .sel(SET));
endmodule

module UC (
  input  UC5,
  input  UC4,
  input  UC3,
  input  UC2,
  input  UC1,
  input  UC0,
  output REGDEST,
  output JUMP,
  output BRANCH,
  output MEMTOREG,
  output ULA0P0,
  output ULA0P1,
  output ULAOPSRC,
  output MEM_WR,
  output ULASRC,
  output WR,
  output TYPE,
  output SET
);

  wire and_2_out, and_3_out, and_4_out, and_5_out, and_6_out, and_7_out, and_8_out, and_9_out, and_10_out,
       and_11_out, and_12_out, and_13_out, and_14_out, and_15_out, and_16_out, and_17_out, and_18_out,
       and_19_out, and_20_out, and_21_out, and_22_out, and_23_out, and_24_out, and_25_out, and_26_out,
       and_27_out, and_28_out, and_29_out, and_30_out, and_31_out, and_32_out, and_33_out, and_34_out,
       and_35_out, and_36_out, and_37_out, and_38_out, and_39_out, and_40_out, and_41_out, and_42_out,
       and_43_out, and_44_out, and_45_out, and_46_out, and_47_out, and_48_out, and_49_out, and_50_out,
       and_51_out, and_52_out, and_53_out, and_54_out, and_55_out, and_56_out, and_57_out, and_58_out,
       and_59_out, not_1_out, not_2_out, not_3_out, not_4_out, not_5_out, not_6_out, not_7_out, not_8_out,
       not_9_out, not_10_out, not_11_out, not_12_out, not_13_out, not_14_out, not_15_out, not_16_out,
       not_17_out, not_18_out, not_19_out, not_20_out, not_21_out, not_22_out, not_23_out, not_24_out,
       not_25_out, not_26_out, not_27_out, not_28_out, not_29_out, not_30_out, not_31_out, not_32_out,
       not_33_out, not_34_out, not_35_out, not_36_out, not_37_out, not_38_out, not_39_out, not_40_out,
       not_41_out, not_42_out, not_43_out, not_44_out, not_45_out, not_46_out, not_47_out, not_48_out,
       not_49_out, not_50_out, not_51_out, not_52_out, not_53_out, not_54_out, not_55_out, not_56_out,
       not_57_out, not_58_out, not_59_out, not_60_out, not_61_out, not_62_out, not_63_out, not_64_out,
       not_65_out, not_66_out, not_67_out, not_68_out, not_69_out, not_70_out, not_71_out, not_72_out,
       not_73_out, not_74_out, not_75_out, not_76_out, not_77_out, not_78_out, not_79_out, not_80_out,
       not_81_out, not_82_out, not_83_out, not_84_out, not_85_out, not_86_out, not_87_out, not_88_out,
       not_89_out, not_90_out, not_91_out, not_92_out;

  not not_1 (not_1_out, UC3);
  not not_2 (not_2_out, UC2);
  not not_3 (not_3_out, UC1);
  not not_4 (not_4_out, UC0);
  not not_5 (not_5_out, UC3);
  not not_6 (not_6_out, UC1);
  not not_7 (not_7_out, UC0);
  not not_8 (not_8_out, UC5);
  not not_9 (not_9_out, UC4);
  not not_10 (not_10_out, UC3);
  not not_11 (not_11_out, UC0);
  not not_12 (not_12_out, UC5);
  not not_13 (not_13_out, UC4);
  not not_14 (not_14_out, UC2);
  not not_15 (not_15_out, UC5);
  not not_16 (not_16_out, UC4);
  not not_17 (not_17_out, UC3);
  not not_18 (not_18_out, UC1);
  not not_19 (not_19_out, UC5);
  not not_20 (not_20_out, UC4);
  not not_21 (not_21_out, UC2);
  not not_22 (not_22_out, UC1);
  not not_23 (not_23_out, UC5);
  not not_24 (not_24_out, UC4);
  not not_25 (not_25_out, UC2);
  not not_26 (not_26_out, UC1);
  not not_27 (not_27_out, UC0);
  not not_28 (not_28_out, UC3);
  not not_29 (not_29_out, UC2);
  not not_30 (not_30_out, UC0);
  not not_31 (not_31_out, UC3);
  not not_32 (not_32_out, UC1);
  not not_33 (not_33_out, UC0);
  not not_34 (not_34_out, UC0);
  not not_35 (not_35_out, UC1);
  not not_36 (not_36_out, UC0);
  not not_37 (not_37_out, UC1);
  not not_38 (not_38_out, UC3);
  not not_39 (not_39_out, UC2);
  not not_40 (not_40_out, UC3);
  not not_41 (not_41_out, UC1);
  not not_42 (not_42_out, UC2);
  not not_43 (not_43_out, UC1);
  not not_44 (not_44_out, UC2);
  not not_45 (not_45_out, UC1);
  not not_46 (not_46_out, UC3);
  not not_47 (not_47_out, UC3);
  not not_48 (not_48_out, UC2);
  not not_49 (not_49_out, UC3);
  not not_50 (not_50_out, UC1);
  not not_51 (not_51_out, UC2);
  not not_52 (not_52_out, UC1);
  not not_53 (not_53_out, UC2);
  not not_54 (not_54_out, UC1);
  not not_55 (not_55_out, UC0);
  not not_56 (not_56_out, UC3);
  not not_57 (not_57_out, UC2);
  not not_58 (not_58_out, UC3);
  not not_59 (not_59_out, UC2);
  not not_60 (not_60_out, UC3);
  not not_61 (not_61_out, UC3);
  not not_62 (not_62_out, UC1);
  not not_63 (not_63_out, UC0);
  not not_64 (not_64_out, UC5);
  not not_65 (not_65_out, UC4);
  not not_66 (not_66_out, UC2);
  not not_67 (not_67_out, UC1);
  not not_68 (not_68_out, UC0);
  not not_69 (not_69_out, UC5);
  not not_70 (not_70_out, UC4);
  not not_71 (not_71_out, UC3);
  not not_72 (not_72_out, UC2);
  not not_73 (not_73_out, UC5);
  not not_74 (not_74_out, UC4);
  not not_75 (not_75_out, UC3);
  not not_76 (not_76_out, UC1);
  not not_77 (not_77_out, UC0);
  not not_78 (not_78_out, UC5);
  not not_79 (not_79_out, UC4);
  not not_80 (not_80_out, UC2);
  not not_81 (not_81_out, UC0);
  not not_82 (not_82_out, UC5);
  not not_83 (not_83_out, UC4);
  not not_84 (not_84_out, UC3);
  not not_85 (not_85_out, UC5);
  not not_86 (not_86_out, UC4);
  not not_87 (not_87_out, UC1);
  not not_88 (not_88_out, UC5);
  not not_89 (not_89_out, UC4);
  not not_90 (not_90_out, UC2);
  not not_91 (not_91_out, UC2);
  not not_92 (not_92_out, UC1);
  and and_1 (SET, UC3, UC2);
  and and_2 (and_2_out, not_1_out, not_2_out, not_3_out, not_4_out);
  and and_3 (and_3_out, not_5_out, UC2, not_6_out, UC0);
  and and_4 (and_4_out, UC3, UC2, not_7_out);
  and and_5 (and_5_out, UC3, UC2, UC1);
  and and_6 (and_6_out, not_8_out, not_9_out, not_10_out, UC2, UC1, not_11_out);
  and and_7 (and_7_out, not_12_out, not_13_out, UC3, not_14_out, UC1);
  and and_8 (and_8_out, not_15_out, not_16_out, not_17_out, UC2, not_18_out, UC0);
  and and_9 (and_9_out, not_19_out, not_20_out, UC3, not_21_out, not_22_out, UC0);
  and and_10 (and_10_out, UC2, UC1, UC0);
  and and_11 (and_11_out, not_23_out, not_24_out, UC3, not_25_out, not_26_out, not_27_out);
  and and_12 (and_12_out, UC3, UC2, UC1);
  and and_13 (and_13_out, UC4, UC2, UC1);
  and and_14 (and_14_out, UC5, UC2, UC1);
  and and_15 (and_15_out, not_28_out, not_29_out, UC1, not_30_out);
  and and_16 (and_16_out, not_31_out, UC2, not_32_out);
  and and_17 (and_17_out, UC3, UC2, UC1, not_33_out);
  and and_18 (and_18_out, UC4, UC1, not_34_out);
  and and_19 (and_19_out, UC4, UC2, not_35_out);
  and and_20 (and_20_out, UC5, UC1, not_36_out);
  and and_21 (and_21_out, UC5, UC2, not_37_out);
  and and_22 (and_22_out, not_38_out, not_39_out, UC1, UC0);
  and and_23 (and_23_out, not_40_out, UC2, not_41_out);
  and and_24 (and_24_out, UC4, not_42_out, UC1, UC0);
  and and_25 (and_25_out, UC4, UC2, not_43_out);
  and and_26 (and_26_out, UC5, not_44_out, UC1, UC0);
  and and_27 (and_27_out, UC5, UC2, not_45_out);
  and and_28 (and_28_out, not_46_out, UC0);
  and and_29 (and_29_out, not_47_out, not_48_out, UC1);
  and and_30 (and_30_out, not_49_out, UC2, not_50_out);
  and and_31 (and_31_out, UC3, not_51_out, not_52_out);
  and and_32 (and_32_out, UC3, UC2, UC1);
  and and_33 (and_33_out, UC4, UC2);
  and and_34 (and_34_out, UC4, UC3);
  and and_35 (and_35_out, UC5, UC1);
  and and_36 (and_36_out, UC5, UC2);
  and and_37 (and_37_out, UC3, not_53_out, not_54_out, not_55_out);
  and and_38 (and_38_out, UC3, UC2, UC1);
  and and_39 (and_39_out, UC4, UC3);
  and and_40 (and_40_out, UC5, UC3);
  and and_41 (and_41_out, not_56_out, not_57_out, UC0);
  and and_42 (and_42_out, not_58_out, not_59_out, UC1);
  and and_43 (and_43_out, not_60_out, UC1, UC0);
  and and_44 (and_44_out, not_61_out, UC2, not_62_out, not_63_out);
  and and_45 (and_45_out, not_64_out, not_65_out, UC3, not_66_out, not_67_out, not_68_out);
  and and_46 (and_46_out, UC3, UC2, UC0);
  and and_47 (and_47_out, UC4, UC0);
  and and_48 (and_48_out, UC4, UC1);
  and and_49 (and_49_out, UC4, UC2);
  and and_50 (and_50_out, UC5, UC0);
  and and_51 (and_51_out, UC5, UC1);
  and and_52 (and_52_out, UC5, UC2);
  and and_53 (and_53_out, not_69_out, not_70_out, not_71_out, not_72_out);
  and and_54 (and_54_out, not_73_out, not_74_out, not_75_out, not_76_out, not_77_out);
  and and_55 (and_55_out, not_78_out, not_79_out, not_80_out, UC1, not_81_out);
  and and_56 (and_56_out, not_82_out, not_83_out, not_84_out, UC1, UC0);
  and and_57 (and_57_out, not_85_out, not_86_out, UC3, UC2, not_87_out);
  and and_58 (and_58_out, not_88_out, not_89_out, UC3, not_90_out, UC0);
  and and_59 (and_59_out, UC3, not_91_out, not_92_out, UC0);
  or or_1 (REGDEST, and_2_out, and_3_out, and_4_out, and_5_out, UC4, UC5);
  or or_2 (JUMP, and_6_out, and_7_out);
  or or_3 (BRANCH, and_8_out, and_9_out);
  or or_4 (MEMTOREG, and_10_out, and_11_out, and_12_out, and_13_out, and_14_out);
  or or_5 (ULA0P0, and_15_out, and_16_out, and_17_out, and_18_out, and_19_out, and_20_out, and_21_out);
  or or_6 (ULA0P1, and_22_out, and_23_out, and_24_out, and_25_out, and_26_out, and_27_out);
  or or_7 (ULAOPSRC, and_28_out, and_29_out, and_30_out, and_31_out, and_32_out, and_33_out, and_34_out, and_35_out, and_36_out);
  or or_8 (MEM_WR, and_37_out, and_38_out, and_39_out, and_40_out);
  or or_9 (WR, and_53_out, and_54_out, and_55_out, and_56_out, and_57_out);
  or or_10 (TYPE, and_58_out, and_59_out);
  or or_11 (ULASRC, and_41_out, and_42_out, and_43_out, and_44_out, and_45_out, and_46_out, and_47_out, and_48_out, and_49_out, and_50_out, and_51_out, and_52_out);
endmodule

// ULAOP
module OPULA (
  input  OPCOD0,
  input  OPCOD1,
  input  OPCOD2,
  input  OPCOD3,
  input  OPCOD4,
  input  OPCOD5,
  input  FUNC0,
  input  FUNC1,
  input  FUNC2,
  input  FUNC3,
  input  FUNC4,
  input  FUNC5,
  output ULAOP0,
  output ULAOP1,
  output ULAOP2,
  output ULAOP3
);
endmodule

// UC
module UC_W (
  input  [5:0] in_1,
  output REGDEST,
  output JUMP,
  output BRANCH,
  output MEMTOREG,
  output [2:0] ALUOP,
  output MEMWRITE,
  output ALUSRC,
  output REGWRITE,
  output TYPE,
  output SET
);

  UC uc_1 (
    .UC5(in_1[5]), .UC4(in_1[4]), .UC3(in_1[3]), .UC2(in_1[2]), .UC1(in_1[1]), .REGDEST(REGDEST),
    .UC0(in_1[0]), .JUMP(JUMP), .BRANCH(BRANCH), .MEMTOREG(MEMTOREG), .ULA0P0(ALUOP[0]), .ULA0P1(ALUOP[1]),
    .ULAOPSRC(ALUOP[2]), .MEM_WR(MEMWRITE), .ULASRC(ALUSRC), .WR(REGWRITE), .TYPE(TYPE), .SET(SET));
endmodule

// ALUCONTROL
module ALU_CONTROL (
  input  [5:0] in_1,
  input  [2:0] in_2,
  output [5:0] out_3
);

  wire [5:0] bit_extender_1_out;

  assign bit_extender_1_out = {{4{1'b0}}, in_2[1:0]};  // Bit_Extender bit_extender_1
  Multiplexer #(.width(6), .enable("false")) multiplexer_1 (
    .in0(in_1), .in1(bit_extender_1_out), .out(out_3), .sel(in_2[2]));
endmodule

module REG_IF_ID (
  input  [31:0] in_1,
  input  [31:0] in_2,
  input  CANADVANCE,
  input  CLK,
  output [31:0] out_5,
  output [31:0] out_6
);

  wire and_1_out;

  Register #(.width(32), .Select("low")) register_1 (.D(in_1), .Q(out_5), .clk(and_1_out));  // open: en, clr
  Register #(.width(32), .Select("low")) register_2 (.D(in_2), .Q(out_6), .clk(and_1_out));  // open: en, clr
  and and_1 (and_1_out, CANADVANCE, CLK);
endmodule

module REG_ID_EX (
  input  RegDest,
  input  Branch,
  input  MemtoReg,
  input  [2:0] ALUOp,
  input  MemWrite,
  input  ALUSrc,
  input  RegWrite,
  input  [31:0] PC_4,
  input  [31:0] DATA_RS,
  input  [31:0] DATA_RT,
  input  [31:0] IMEXT,
  input  [4:0] RT,
  input  [4:0] RD,
  input  TYPE,
  input  [31:0] LABEL,
  input  JUMP,
  input  SET,
  input  [4:0] RS,
  input  [31:0] INS,
  input  CanAdvance,
  input  CLK,
  output RegDest_2,
  output Branch_2,
  output MemtoReg_2,
  output [2:0] ALUOp_2,
  output MemWrite_2,
  output ALUSrc_2,
  output RegWrite_2,
  output [31:0] PC_4_2,
  output [31:0] DATA_RS_2,
  output [31:0] DATA_RT_2,
  output [31:0] IMEXT_2,
  output [4:0] RT_2,
  output [4:0] RD_2,
  output TYPE_2,
  output [31:0] LABEL_2,
  output JUMP_2,
  output SET_2,
  output [4:0] RS_2,
  output [31:0] INS_2
);

  wire and_1_out;

  Register #(.width(1), .Select("low")) register_1 (.D(RegDest), .Q(RegDest_2), .clk(and_1_out));  // open: en, clr
  Register #(.width(1), .Select("low")) register_2 (.D(Branch), .Q(Branch_2), .clk(and_1_out));  // open: en, clr
  Register #(.width(1), .Select("low")) register_3 (.D(MemtoReg), .Q(MemtoReg_2), .clk(and_1_out));  // open: en, clr
  Register #(.width(3), .Select("low")) register_4 (.D(ALUOp), .Q(ALUOp_2), .clk(and_1_out));  // open: en, clr
  Register #(.width(1), .Select("low")) register_5 (.D(MemWrite), .Q(MemWrite_2), .clk(and_1_out));  // open: en, clr
  Register #(.width(1), .Select("low")) register_6 (.D(ALUSrc), .Q(ALUSrc_2), .clk(and_1_out));  // open: en, clr
  Register #(.width(1), .Select("low")) register_7 (.D(RegWrite), .Q(RegWrite_2), .clk(and_1_out));  // open: en, clr
  Register #(.width(32), .Select("low")) register_8 (.D(PC_4), .Q(PC_4_2), .clk(and_1_out));  // open: en, clr
  Register #(.width(32), .Select("low")) register_9 (.D(DATA_RS), .Q(DATA_RS_2), .clk(and_1_out));  // open: en, clr
  Register #(.width(32), .Select("low")) register_10 (.D(DATA_RT), .Q(DATA_RT_2), .clk(and_1_out));  // open: en, clr
  Register #(.width(32), .Select("low")) register_11 (.D(IMEXT), .Q(IMEXT_2), .clk(and_1_out));  // open: en, clr
  Register #(.width(5), .Select("low")) register_12 (.D(RT), .Q(RT_2), .clk(and_1_out));  // open: en, clr
  Register #(.width(5), .Select("low")) register_13 (.D(RD), .Q(RD_2), .clk(and_1_out));  // open: en, clr
  Register #(.width(1), .Select("low")) register_14 (.D(TYPE), .Q(TYPE_2), .clk(and_1_out));  // open: en, clr
  Register #(.width(32), .Select("low")) register_15 (.D(LABEL), .Q(LABEL_2), .clk(and_1_out));  // open: en, clr
  Register #(.width(1), .Select("low")) register_16 (.D(JUMP), .Q(JUMP_2), .clk(and_1_out));  // open: en, clr
  Register #(.width(1), .Select("low")) register_17 (.D(SET), .Q(SET_2), .clk(and_1_out));  // open: en, clr
  Register #(.width(5), .Select("low")) register_18 (.D(RS), .Q(RS_2), .clk(and_1_out));  // open: en, clr
  Register #(.width(32), .Select("low")) register_19 (.D(INS), .Q(INS_2), .clk(and_1_out));  // open: en, clr
  and and_1 (and_1_out, CanAdvance, CLK);
endmodule

module REG_EX_MEM (
  input  BRANCH,
  input  MEMTOREG,
  input  MEMORY_WRITE,
  input  REGWRITE,
  input  [31:0] BRANCH_ADDRESS,
  input  zero,
  input  [31:0] ALU_OUT,
  input  [31:0] DATA_RT,
  input  [4:0] WRITE_REGISTER,
  input  TYPE,
  input  [31:0] LABEL,
  input  JUMP,
  input  [31:0] PC_4,
  input  [31:0] INS,
  input  Clear,
  input  CanAdvance,
  input  CLK,
  output BRANCH_2,
  output MEMTOREG_2,
  output MEMORY_WRITE_2,
  output REGWRITE_2,
  output [31:0] BRANCH_ADDRESS_2,
  output zero_2,
  output [31:0] ALU_OUT_2,
  output [31:0] DATA_RT_2,
  output [4:0] WRITE_REGISTER_2,
  output TYPE_2,
  output [31:0] LABEL_2,
  output JUMP_2,
  output [31:0] PC_4_2,
  output [31:0] INS_2
);

  wire and_1_out;

  Register #(.width(1), .Select("low")) register_1 (
    .D(BRANCH), .Q(BRANCH_2), .clk(and_1_out), .clr(Clear));  // open: en
  Register #(.width(1), .Select("low")) register_2 (
    .D(MEMTOREG), .Q(MEMTOREG_2), .clk(and_1_out), .clr(Clear));  // open: en
  Register #(.width(1), .Select("low")) register_3 (
    .D(MEMORY_WRITE), .Q(MEMORY_WRITE_2), .clk(and_1_out), .clr(Clear));  // open: en
  Register #(.width(1), .Select("low")) register_4 (
    .D(REGWRITE), .Q(REGWRITE_2), .clk(and_1_out), .clr(Clear));  // open: en
  Register #(.width(32), .Select("low")) register_5 (
    .D(BRANCH_ADDRESS), .Q(BRANCH_ADDRESS_2), .clk(and_1_out), .clr(Clear));  // open: en
  Register #(.width(1), .Select("low")) register_6 (.D(zero), .Q(zero_2), .clk(and_1_out), .clr(Clear));  // open: en
  Register #(.width(32), .Select("low")) register_7 (
    .D(ALU_OUT), .Q(ALU_OUT_2), .clk(and_1_out), .clr(Clear));  // open: en
  Register #(.width(32), .Select("low")) register_8 (
    .D(DATA_RT), .Q(DATA_RT_2), .clk(and_1_out), .clr(Clear));  // open: en
  Register #(.width(5), .Select("low")) register_9 (
    .D(WRITE_REGISTER), .Q(WRITE_REGISTER_2), .clk(and_1_out), .clr(Clear));  // open: en
  Register #(.width(1), .Select("low")) register_10 (.D(TYPE), .Q(TYPE_2), .clk(and_1_out), .clr(Clear));  // open: en
  Register #(.width(32), .Select("low")) register_11 (
    .D(LABEL), .Q(LABEL_2), .clk(and_1_out), .clr(Clear));  // open: en
  Register #(.width(1), .Select("low")) register_12 (.D(JUMP), .Q(JUMP_2), .clk(and_1_out), .clr(Clear));  // open: en
  Register #(.width(32), .Select("low")) register_13 (.D(PC_4), .Q(PC_4_2), .clk(and_1_out), .clr(Clear));  // open: en
  Register #(.width(32), .Select("low")) register_14 (.D(INS), .Q(INS_2), .clk(and_1_out), .clr(Clear));  // open: en
  and and_1 (and_1_out, CanAdvance, CLK);
endmodule

module REG_MEM_WB (
  input  [31:0] PC_4,
  input  REG_WRITE,
  input  MEMTOREG,
  input  [31:0] MEM_OUT,
  input  [31:0] ALU_OUT,
  input  [4:0] WRITE_REGISTER,
  input  JUMP,
  input  [31:0] INS,
  input  CLK,
  output [31:0] PC_4_2,
  output REG_WRITE_2,
  output MEMTOREG_2,
  output [31:0] MEM_OUT_2,
  output [31:0] ALU_OUT_2,
  output [4:0] WRITE_REGISTER_2,
  output JUMP_2,
  output [31:0] INS_2
);

  Register #(.width(32), .Select("low")) register_1 (.D(PC_4), .Q(PC_4_2), .clk(CLK));  // open: en, clr
  Register #(.width(1), .Select("low")) register_2 (.D(REG_WRITE), .Q(REG_WRITE_2), .clk(CLK));  // open: en, clr
  Register #(.width(1), .Select("low")) register_3 (.D(MEMTOREG), .Q(MEMTOREG_2), .clk(CLK));  // open: en, clr
  Register #(.width(32), .Select("low")) register_4 (.D(MEM_OUT), .Q(MEM_OUT_2), .clk(CLK));  // open: en, clr
  Register #(.width(32), .Select("low")) register_5 (.D(ALU_OUT), .Q(ALU_OUT_2), .clk(CLK));  // open: en, clr
  Register #(.width(5), .Select("low")) register_6 (
    .D(WRITE_REGISTER), .Q(WRITE_REGISTER_2), .clk(CLK));  // open: en, clr
  Register #(.width(1), .Select("low")) register_7 (.D(JUMP), .Q(JUMP_2), .clk(CLK));  // open: en, clr
  Register #(.width(32), .Select("low")) register_8 (.D(INS), .Q(INS_2), .clk(CLK));  // open: en, clr
endmodule

module Branch_Jump_Unit (
  input  TYPE,
  input  EQUAL,
  input  BRANCH,
  input  [31:0] IMADDRESS,
  input  [31:0] LABELADDRESS,
  input  JUMP,
  output PCMUX,
  output [31:0] ADDRESS
);

  wire and_1_out, and_2_out, and_3_out, and_4_out, or_1_out;

  and and_1 (and_1_out, EQUAL, ~TYPE);  // AND_Gate
  and and_2 (and_2_out, ~EQUAL, TYPE);  // AND_Gate
  or or_1 (or_1_out, and_1_out, and_2_out);
  and and_3 (and_3_out, or_1_out, BRANCH);
  or or_2 (PCMUX, and_3_out, JUMP);
  and and_4 (and_4_out, JUMP, ~TYPE);  // AND_Gate
  Multiplexer #(.width(32), .enable("false")) multiplexer_1 (
    .in0(IMADDRESS), .in1(LABELADDRESS), .out(ADDRESS), .sel(and_4_out));
endmodule

module Hazard_Unit (
  input  REGWRITE_MEM_WB,
  input  REGWRITE_EX_MEM,
  input  MEMTOREG_EX_MEM,
  input  [4:0] WR_EX_MEM,
  input  [4:0] WR_MEM_WB,
  input  [4:0] RS_ID,
  input  [4:0] RT_ID,
  input  CLK,
  input  [31:0] ALUOUT_EX_MEM,
  input  [31:0] DATAOUT_MEM_WB,
  input  [31:0] INS,
  input  [31:0] INS_EX_MEM,
  input  [31:0] INS_MEM_WB,
  output RS_DATA_SRC,
  output RT_DATA_SRC,
  output CAN_ADVANCE,
  output CLEAR_EX_MEM__NOP,
  output HAZARD_DETECTED,
  output [31:0] FIXED_DATA_RS,
  output [31:0] FIXED_DATA_RT
);

  wire and_1_out, and_2_out, and_3_out, and_4_out, and_5_out, and_6_out, comparator_1_eq, comparator_2_eq,
       comparator_3_eq, comparator_4_eq, comparator_5_eq, comparator_6_eq, comparator_7_eq, NOP, not_1_out,
       or_1_out, or_2_out, or_3_out, or_4_out, or_6_out, register_1_q;

  Comparator #(.width(5)) comparator_1 (.a(RS_ID), .b(WR_EX_MEM), .eq(comparator_1_eq));  // open: gt, lt
  Comparator #(.width(5)) comparator_2 (.a(RT_ID), .b(WR_EX_MEM), .eq(comparator_2_eq));  // open: gt, lt
  Comparator #(.width(5)) comparator_3 (.a(RS_ID), .b(WR_MEM_WB), .eq(comparator_3_eq));  // open: gt, lt
  Comparator #(.width(5)) comparator_4 (.a(RT_ID), .b(WR_MEM_WB), .eq(comparator_4_eq));  // open: gt, lt
  or or_1 (or_1_out, comparator_1_eq, comparator_3_eq);
  or or_2 (or_2_out, comparator_2_eq, comparator_4_eq);
  or or_3 (or_3_out, comparator_1_eq, comparator_2_eq);
  and and_1 (and_1_out, REGWRITE_MEM_WB, or_4_out);
  or or_4 (or_4_out, comparator_3_eq, comparator_4_eq);
  and and_2 (and_2_out, REGWRITE_EX_MEM, or_3_out);
  and and_3 (and_3_out, ~comparator_1_eq, comparator_3_eq);  // AND_Gate
  and and_4 (and_4_out, ~comparator_2_eq, comparator_4_eq);  // AND_Gate
  Comparator #(.width(32), .mode("unsigned")) comparator_5 (
    .a(INS), .b({32{1'b0}}), .eq(comparator_5_eq));  // open: gt, lt
  Comparator #(.width(32), .mode("unsigned")) comparator_6 (
    .a({32{1'b0}}), .b(INS_EX_MEM), .eq(comparator_6_eq));  // open: gt, lt
  Comparator #(.width(32), .mode("unsigned")) comparator_7 (
    .a({32{1'b0}}), .b(INS_MEM_WB), .eq(comparator_7_eq));  // open: gt, lt
  Multiplexer #(.width(32), .enable("false")) multiplexer_1 (
    .in0(ALUOUT_EX_MEM), .in1(DATAOUT_MEM_WB), .out(FIXED_DATA_RS), .sel(and_3_out));
  and and_5 (and_5_out, comparator_6_eq, comparator_7_eq);
  Multiplexer #(.width(32), .enable("false")) multiplexer_2 (
    .in0(ALUOUT_EX_MEM), .in1(DATAOUT_MEM_WB), .out(FIXED_DATA_RT), .sel(and_4_out));
  or or_5 (NOP, comparator_5_eq, and_5_out);
  not not_1 (not_1_out, and_6_out);
  and and_6 (and_6_out, and_2_out, MEMTOREG_EX_MEM);
  or or_6 (or_6_out, and_2_out, and_1_out);
  and and_7 (RS_DATA_SRC, or_1_out, not_1_out);
  and and_8 (RT_DATA_SRC, or_2_out, not_1_out);
  and and_9 (HAZARD_DETECTED, or_6_out, ~NOP);  // AND_Gate
  Register #(.width(1), .trigger("falling"), .Select("low")) register_1 (
    .D(and_6_out), .Q(register_1_q), .clk(CLK));  // open: en, clr
  not not_2 (CAN_ADVANCE, register_1_q);
  and and_10 (CLEAR_EX_MEM__NOP, register_1_q, CLK);

  // Notes on the sheet:
  //   DEBUG
  //   DEBUG
endmodule
